// Logisim project Single_Cycle_CPU.circ as structural Verilog: 1 circuit, main circuit main
module main (
);

  wire and_1_out, Clk, clock_1_out, ExRegWrite, Halt, HasExp, IsCOP0, isJAL, IsRet, multiplexer_4_out,
       not_2_out, not_3_out, not_4_out, or_1_out, undriven_2;
  wire [7:0] undriven_4;
  wire [31:0] adder_1_out, multiplexer_1_out, multiplexer_2_out, multiplexer_6_out, multiplexer_7_out,
       ram_1_dout, register_2_q, undriven, undriven_3, undriven_5;

  Multiplexer #(.width(32)) multiplexer_1 (.in1(undriven), .out(multiplexer_1_out), .sel(and_1_out));  // open: in0
  and and_1 (and_1_out, IsRet, IsCOP0);
  Clock clock_1 (.out(clock_1_out));
  Multiplexer #(.width(32)) multiplexer_2 (
    .in0({32{1'b0}}), .in1(multiplexer_1_out), .out(multiplexer_2_out), .sel(HasExp));
  not not_1 (HasExp, undriven_2);
  Multiplexer multiplexer_3 (.in0(clock_1_out), .in1(1'b0), .out(Clk), .sel(Halt));
  Register #(.width(32)) register_1 (.D(multiplexer_2_out), .clk(multiplexer_4_out));  // open: en, Q, clr
  Multiplexer multiplexer_4 (.in0(Clk), .in1(not_2_out), .out(multiplexer_4_out), .sel(or_1_out));
  or or_1 (or_1_out, undriven_2, and_1_out);
  not not_2 (not_2_out, Clk);
  Adder #(.width(32)) adder_1 (.b({32{1'b0}}), .out(adder_1_out));  // open: a, cin, cout
  Register #(.width(32)) register_2 (.Q(register_2_q), .clk(HasExp));  // open: D, en, clr
  // control_unit control_unit_1: pin names not known
  // CP0 cp0_1: pin names not known; wires that end beside it: Clk, HasExp, ExRegWrite
  Multiplexer #(.width(32)) multiplexer_5 (.in0(undriven_3), .in1(multiplexer_6_out), .sel(not_3_out));  // open: out
  not not_3 (not_3_out, IsCOP0);
  not not_4 (not_4_out, isJAL);
  Multiplexer #(.width(32)) multiplexer_6 (
    .in0(adder_1_out), .in1(multiplexer_7_out), .out(multiplexer_6_out), .sel(not_4_out));
  RAM #(.dataWidth(32)) ram_1 (.addr(undriven_4), .dout(ram_1_dout));  // open: we, oe, clk, din
  Multiplexer #(.width(32)) multiplexer_7 (.in0(undriven_5), .in1(ram_1_dout), .out(multiplexer_7_out), .sel(IsCOP0));

  // Notes on the sheet:
  //   PC Buffer
endmodule
